# Fritzing sketch Wakie (saved by Fritzing 0.9.10b)
breadboards: 3

parts:
  LCD1 = LCD screen
  Part1 = Arduino Nano (Rev3.0)
  Part2 = Adafruit DS1307 RTC Breakout [part_number="Adafruit #264"]
  J1 = Piezo Speaker
  S1 = Pushbutton [package="[THT]"]
  R1 = Resistor [tolerance=±5% power=0.25 resistance=220 package=THT]
  R2 = Resistor [tolerance=±5% power=0.25 resistance=1k package=THT]
  Q1 = NPN-Transistor [package="TO92 [THT]"]
  R3 = Resistor [tolerance=±5% power=0.25 resistance=100k package=THT]

nets:
  GND: LCD1.VSS, LCD1.V0, LCD1.R/W, LCD1.LED-, Part1.GND, Part2.GND, J1.pin1, R1.Pin_1
  VDD: LCD1.VDD, Part1.5V, Part2.VCC, S1.Pin_3, S1.Pin_4, Q1.C
  N1: LCD1.RS, Part1.D4
  N2: LCD1.E, Part1.D5
  N3: LCD1.DB4, Part1.D6
  N4: LCD1.DB5, Part1.D7
  N5: LCD1.DB6, Part1.D8
  N6: LCD1.DB7, Part1.D9
  N7: LCD1.LED+, R2.Pin_0
  N8: Part1.D10, R3.Pin_1
  N9: Part1.D11/MOSI, J1.pin2
  N10: Part1.D12/MISO, S1.Pin_1, S1.Pin_2, R1.Pin_0
  N11: Part1.A5, Part2.SCL
  N12: Part1.A4, Part2.SDA
  N13: R2.Pin_1, Q1.E
  N14: Q1.B, R3.Pin_0

custom parts:
  Adafruit DS1307 RTC Breakout: This is a great battery-backed real time clock (RTC) that allows your microcontroller project to keep track of time even if it is reprogrammed, or if the power is lost. Perfect for datalogging, clock-building, time stamping, timers and alarms, etc. The DS1307 is the most popular RTC - but it requires 5V power to work (although we've used it with 5V power and 3.3V logic successfully) PCB &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
